# Fritzing sketch Block_diagram (saved by Fritzing 0.9.9b)

parts:
  Part1 = Arduino Uno (Rev3) - ICSP
  Part2 = BME280
  Grove1 = Grove OLED 128x96
  INA1 = INA219 DC Current Sensor Breakout
  R1 = Resistor [tolerance=±5% power=0.25 resistance=220 package=THT]  # not connected
  R2 = Resistor [tolerance=±5% power=0.25 resistance=220 package=THT]  # not connected

nets:
  N1: Part1.A4/SDA, Part2.SDA, Grove1.SDA, INA1.SDA
  N2: Part1.A5/SCL, Part2.SCL, Grove1.SCL, INA1.SCL
  VCC: Part1.5V, Part2.VIN, Grove1.VCC, INA1.VCC
  GND: Part1.GND, Part2.GND, Grove1.GND, INA1.GND

custom parts:
  INA219 DC Current Sensor Breakout: INA DC Current Sensor Breakout
